// Logisim project assignment_4.circ as structural Verilog
module main (
);

  wire vote25_1_result;
  wire [24:0] dipswitch_1_sw25;

  DipSwitch #(.number(25)) dipswitch_1 (
    .sw1(dipswitch_1_sw25[24]), .sw2(dipswitch_1_sw25[23]), .sw3(dipswitch_1_sw25[22]),
    .sw4(dipswitch_1_sw25[21]), .sw5(dipswitch_1_sw25[20]), .sw6(dipswitch_1_sw25[19]),
    .sw7(dipswitch_1_sw25[18]), .sw8(dipswitch_1_sw25[17]), .sw9(dipswitch_1_sw25[16]),
    .sw10(dipswitch_1_sw25[15]), .sw11(dipswitch_1_sw25[14]), .sw12(dipswitch_1_sw25[13]),
    .sw13(dipswitch_1_sw25[12]), .sw14(dipswitch_1_sw25[11]), .sw15(dipswitch_1_sw25[10]),
    .sw16(dipswitch_1_sw25[9]), .sw17(dipswitch_1_sw25[8]), .sw18(dipswitch_1_sw25[7]),
    .sw19(dipswitch_1_sw25[6]), .sw20(dipswitch_1_sw25[5]), .sw21(dipswitch_1_sw25[4]),
    .sw22(dipswitch_1_sw25[3]), .sw23(dipswitch_1_sw25[2]), .sw24(dipswitch_1_sw25[1]),
    .sw25(dipswitch_1_sw25[0]));
  vote25 vote25_1 (.vt(dipswitch_1_sw25), .result(vote25_1_result));
  LED led_1 (.in(vote25_1_result));
endmodule

// VHDL entity vote25, as the project stores it:
library ieee;
use ieee.std_logic_1164.all;
use ieee.std_logic_arith.all;
use ieee.std_logic_unsigned.all;

--entity
entity vote25 is
    port (
        vt : in std_logic_vector(25 downto 1);
        result : out std_logic
    );
end entity vote25;

--architecture
architecture bhv of vote25 is
begin
    process(vt)
        variable sum : integer range 0 to 25;
    begin
        sum := 0;
        for i in 1 to 25 loop
            if (vt(i) = '1') then
                sum := sum + 1;
                if sum >= 13 then
                    result <= '1';
                else
                    result <= '0';
                end if;
            end if;
        end loop;
    end process;
end architecture bhv;
