// Logisim project assignment_5.circ as structural Verilog
module main (
  input  in_1
);

  wire [7:0] led_1_display;
  wire [14:0] dipswitch_1_sw15;

  DipSwitch #(.number(15)) dipswitch_1 (
    .sw1(dipswitch_1_sw15[14]), .sw2(dipswitch_1_sw15[13]), .sw3(dipswitch_1_sw15[12]),
    .sw4(dipswitch_1_sw15[11]), .sw5(dipswitch_1_sw15[10]), .sw6(dipswitch_1_sw15[9]),
    .sw7(dipswitch_1_sw15[8]), .sw8(dipswitch_1_sw15[7]), .sw9(dipswitch_1_sw15[6]),
    .sw10(dipswitch_1_sw15[5]), .sw11(dipswitch_1_sw15[4]), .sw12(dipswitch_1_sw15[3]),
    .sw13(dipswitch_1_sw15[2]), .sw14(dipswitch_1_sw15[1]), .sw15(dipswitch_1_sw15[0]));
  _7_Segment_Display u_7_segment_display_1 (
    .g(led_1_display[1]), .f(led_1_display[2]), .a(led_1_display[7]), .b(led_1_display[6]),
    .e(led_1_display[3]), .d(led_1_display[4]), .c(led_1_display[5]), .dp(led_1_display[0]));
  led led_1 (.en(in_1), .vt(dipswitch_1_sw15), .display(led_1_display));
endmodule

// VHDL entity led, as the project stores it:
library ieee;
use ieee.std_logic_1164.all;

entity led is
    port (
        en : in  std_logic;
        vt : in  std_logic_vector(15 downto 1);
        display : out std_logic_vector(7 downto 0)
    );
end entity led;

architecture bhv of led is
begin
    process(en, vt)
        variable sum : integer range 0 to 15;
    begin
        if en = '0' then
            display <= "ZZZZZZZZ";
        else
            sum := 0;
            for i in 1 to 15 loop
                if vt(i) = '1' then
                    sum := sum + 1;
                end if;
            end loop;

            case sum is
                when 0 => display <= "11111100"; -- 0
                when 1 => display <= "01100000"; -- 1
                when 2 => display <= "11011010"; -- 2
                when 3 => display <= "11110010"; -- 3
                when 4 => display <= "01100110"; -- 4
                when 5 => display <= "10110110"; -- 5
                when 6 => display <= "10111110"; -- 6
                when 7 => display <= "11100000"; -- 7
                when 8 => display <= "11111110"; -- 8
                when 9 => display <= "11100110"; -- 9
                when 10 => display <= "11101110"; -- A
                when 11 => display <= "00111110"; -- b
                when 12 => display <= "10011100"; -- C
                when 13 => display <= "01111010"; -- d
                when 14 => display <= "10011110"; -- E
                when 15 => display <= "10001110"; -- F
            end case;
        end if;
    end process;
end architecture bhv;
