// Logisim project assignment_3_2.circ as structural Verilog
module main (
  input  d,
  input  in_2,
  input  in_3,
  input  en,
  output q,
  output out_6,
  output nq
);

  wire nand_1_out, nand_2_out, not_1_out;

  not not_1 (not_1_out, d);
  nand nand_1 (nand_1_out, d, en);
  nand nand_2 (nand_2_out, en, not_1_out);
  nand nand_3 (q, nand_1_out, nq);
  nand nand_4 (nq, q, nand_2_out);
  d_latch d_latch_1 (.en(in_2), .d(in_3), .q(out_6));
endmodule

// VHDL entity d_latch, as the project stores it:
LIBRARY ieee;
USE ieee.std_logic_1164.ALL;

ENTITY d_latch IS
PORT (
    en : IN std_logic;
    d  : IN std_logic;
    q  : OUT std_logic
);
END d_latch;

ARCHITECTURE bhv OF d_latch IS
BEGIN

    PROCESS(en, d)
    BEGIN
        IF (en = '1') THEN
            q <= d;
        END IF;
    END PROCESS;

END bhv;
