// Logisim project assignment_3_3.circ as structural Verilog
module main (
  input  d,
  input  clk,
  input  in_3,
  input  in_4,
  output q,
  output nq,
  output out_7,
  output out_8
);

  wire nand_1_out, nand_2_out, nand_3_out, nand_5_out, nand_6_out, not_1_out, not_2_out, not_3_out, not_4_out;

  not not_1 (not_1_out, clk);
  not not_2 (not_2_out, d);
  nand nand_1 (nand_1_out, d, not_1_out);
  nand nand_2 (nand_2_out, not_1_out, not_2_out);
  nand nand_3 (nand_3_out, nand_1_out, out_7);
  nand nand_4 (out_7, nand_3_out, nand_2_out);
  not not_3 (not_3_out, not_1_out);
  not not_4 (not_4_out, nand_3_out);
  nand nand_5 (nand_5_out, nand_3_out, not_3_out);
  nand nand_6 (nand_6_out, not_3_out, not_4_out);
  nand nand_7 (q, nand_5_out, nq);
  nand nand_8 (nq, q, nand_6_out);
  d_flipflop d_flipflop_1 (.clk(in_3), .d(in_4), .q(out_8));

  // Notes on the sheet:
  //   e
endmodule

// VHDL entity d_flipflop, as the project stores it:
LIBRARY ieee;
USE ieee.std_logic_1164.ALL;

ENTITY d_flipflop IS
  PORT (
    clk : IN std_logic;
    d   : IN std_logic;
    q   : OUT std_logic
  );
END d_flipflop;


ARCHITECTURE bhv OF d_flipflop IS
BEGIN
  process(clk)
  BEGIN
    IF (clk'event AND clk = '1') THEN
      q <= d;
    END IF;
  END process;
END bhv;
