// Logisim project assignment_3_4.circ as structural Verilog
module main (
  input  j,
  input  in_2,
  input  in_3,
  input  in_4,
  input  clk,
  input  in_6,
  input  in_7,
  input  clr,
  input  k,
  output q,
  output out_11,
  output nq
);

  wire nand_1_out, nand_2_out, nand_3_out, nand_4_out, nand_5_out, nand_6_out, not_1_out;

  not not_1 (not_1_out, clk);
  nand nand_1 (nand_1_out, nq, j, not_1_out);
  nand nand_2 (nand_2_out, not_1_out, k, q);
  nand nand_3 (nand_3_out, nand_1_out, nand_4_out);
  nand nand_4 (nand_4_out, nand_3_out, nand_2_out);
  nand nand_5 (nand_5_out, clk, nand_3_out);
  nand nand_6 (nand_6_out, nand_4_out, clk);
  nand nand_7 (q, nand_5_out, nq);
  nand nand_8 (nq, q, clr, nand_6_out);
  jk_flipflop jk_flipflop_1 (.clk(in_2), .j(in_3), .k(in_4), .clr(in_6), .set(in_7), .q(out_11));
endmodule

// VHDL entity jk_flipflop, as the project stores it:
LIBRARY ieee;
USE ieee.std_logic_1164.all;
USE ieee.numeric_std.all;

ENTITY jk_flipflop IS
  PORT (
    clk : IN  std_logic;
    j   : IN  std_logic;
    k   : IN  std_logic;
    clr : IN  std_logic;
    set : IN  std_logic;
    q   : OUT std_logic
  );
END ENTITY jk_flipflop;

ARCHITECTURE bhv OF jk_flipflop IS
  SIGNAL q_internal : std_logic := '0';
BEGIN
  q <= q_internal;
  process(clk, clr, set)
  begin
    if clr = '1' then
      q_internal <= '0';
    elsif set = '1' then
      q_internal <= '1';
    elsif (clk'event and clk = '1') then
      if (j = '1' and k = '0') then
        q_internal <= '1';
      elsif (j = '0' and k = '1') then
        q_internal <= '0';
      elsif (j = '1' and k = '1') then
        q_internal <= not q_internal;
      end if;
    end if;
  end process;
END ARCHITECTURE bhv;
